# Fritzing sketch Temperature_Humidity (saved by Fritzing 0.9.3b)
perfboards: 1

parts:
  Part1 = Arduino Nano (Rev3.0)
  R1 = Trimmer Potentiometer [maximum_resistance=10kΩ package=THT]
  LCD1 = LCD screen
  RHT1 = Humidity and Temperature Sensor RHT03
  Power_plug1 = Power plug

nets:
  GND: Part1.GND, LCD1.LED-, Power_plug1.GND
  N1: Part1.D2, LCD1.DB7
  N2: Part1.D3, LCD1.DB6
  N3: Part1.D4, LCD1.DB5
  N4: Part1.D5, LCD1.DB4
  N5: Part1.D8, RHT1.Data-signal
  N6: Part1.D11/MOSI, LCD1.E
  N7: Part1.D12/MISO, LCD1.RS
  VIN: Part1.VIN, LCD1.LED+, Power_plug1.VCC
  N8: R1.wiper, LCD1.V0
